# Fritzing sketch A fritzing (saved by Fritzing 0.9.3b)
breadboards: 1

parts:
  S1 = Pushbutton [package="[THT]"]
  Part1 = Arduino Uno (Rev3)
  S2 = Pushbutton [package="[SMD]"]
  J1 = Basic Servo
  R1 = Resistor [tolerance=±5% resistance=220 package="0805 [SMD]"]
  R2 = Resistor [tolerance=±5% resistance=220 package=THT]

nets:
  5V: S1.Pin_1, S1.Pin_2, Part1.5V, S2.Pin_1, S2.Pin_2, J1.vcc
  N1: S1.Pin_3, S1.Pin_4, Part1.D2, R2.Pin_0
  N2: Part1.D9_PWM, J1.pulse
  N3: Part1.D3_PWM, S2.Pin_3, S2.Pin_4, R1.Pin_0
  GND: Part1.GND, J1.gnd, R1.Pin_1, R2.Pin_1
