# Fritzing sketch Ub fritzinf (saved by Fritzing 0.9.3b)
breadboards: 1

parts:
  Part2 = Arduino Uno (Rev3) - ICSP  # not connected
  Part3 = Arduino ProtoShield
  J1 = Basic Servo
  LED2 = LED - 3mm [color="Red (633nm)" package="3 mm [THT]"]
  R1 = Resistor [tolerance=±5% resistance=220 package="0603 [SMD]"]
  R2 = Resistor [tolerance=±5% resistance=220 package="2512 [SMD]"]
  S1 = Toggle Switch [package=THT]
  S2 = Toggle Switch [package=THT]
  VCC1 = Battery block 9V

nets:
  N1: Part3.5V, Part3.N$108
  N2: Part3.GND, Part3.N$97, R2.Pin_1, S1.L1
  N3: Part3.VIN, VCC1.+
  N4: Part3.D6, Part3.N$151
  N5: Part3.D9, Part3.N$12
  N6: Part3.N$11, J1.pulse
  N7: Part3.N$20, Part3.N$109
  N8: Part3.N$22, J1.vcc
  N9: Part3.N$32, Part3.N$98
  N10: Part3.N$33, J1.gnd
  N11: Part3.N$99, R1.Pin_0
  N12: Part3.N$110, LED2.cathode
  N13: Part3.N$111, S2.L1
  N14: Part3.N$142, LED2.anode
  N15: Part3.N$143, R1.Pin_1
  N16: Part3.N$158, S2.COM
  N17: S1.COM, VCC1.-
