# Fritzing sketch fritzing_UR (saved by Fritzing 0.9.3b)
breadboards: 1

parts:
  Part1 = Arduino Uno (Rev3) - ICSP
  BAT1 = BC9VPC [package=bc9vpc]
  hc-sr1 = hc-sr04
  J2 = Basic Servo
  J1 = Basic Servo

nets:
  VCC: Part1.5V, hc-sr1.VCC, J2.vcc, J1.vcc
  N1: Part1.D8, J1.pulse
  N2: Part1.D9_PWM, J2.pulse
  N3: Part1.D6_PWM, hc-sr1.Trig
  N4: Part1.D7, hc-sr1.Echo
  GND: Part1.GND, BAT1.V-, hc-sr1.GND, J2.gnd, J1.gnd
  N5: Part1.VIN, BAT1.V+
